// Logisim project Lab3_HERA_processor.circ as structural Verilog: 17 circuits, main circuit microprocessor
module microprocessor (
  output [15:0] contents_of_Rd,
  output [15:0] Memory_Address,
  output [15:0] out_3,
  output [4:0] out_4,
  output [7:0] out_5,
  output [15:0] out_6,
  output [15:0] out_7,
  output [15:0] out_8,
  output [15:0] out_9,
  output [4:0] CBCVZSFlags,
  output [4:0] out_11,
  output [15:0] out_12,
  output [4:0] NewALUFlags,
  output [4:0] out_14,
  output [15:0] out_15,
  output [15:0] Current_PC,
  output [15:0] New_PC
);

  wire and_1_out, and_2_out, and_3_out, and_4_out, and_5_out, and_6_out, and_7_out, and_8_out, and_9_out,
       and_10_out, and_11_out, and_12_out, and_13_out, and_14_out, and_15_out, and_16_out, and_17_out,
       and_18_out, and_19_out, and_20_out, and_21_out, and_22_out, and_23_out, and_24_out, Clock,
       comparator_1_eq, comparator_3_eq, comparator_4_eq, comparator_5_eq, comparator_6_eq, comparator_7_eq,
       comparator_8_eq, comparator_9_eq, comparator_10_eq, comparator_11_eq, comparator_12_eq,
       comparator_14_eq, comparator_15_eq, enabled, enabled_Flags_M, enabled_register_file,
       enabled_SaveOrRestore, Flags_out_5, Flags_out_6, Flags_out_7, Flags_out_8, Flags_out_9,
       hardware_Interrupt, IncorDec, Interrupting, IsBranOp, IsCall_Return, isHalt, IsInterrupt, isLoad,
       IsRTI, isStore, Key1Available, Key2Available, keyboardEnabled, keyInput, L_S, NeedToBran, nor_1_out,
       not_1_out, not_2_out, not_3_out, not_4_out, not_5_out, not_6_out, not_7_out, not_8_out, not_9_out,
       not_10_out, not_11_out, not_12_out, not_13_out, not_14_out, not_15_out, not_16_out, not_17_out,
       not_18_out, not_19_out, not_20_out, not_21_out, or_2_out, or_3_out, or_4_out, or_5_out, or_7_out,
       or_8_out, or_9_out, or_10_out, or_13_out, printToScreen, RegisMode_relative, xor_1_out, xor_2_out;
  wire [1:1] IncorDec_Operation;
  wire [2:1] L_S_op;
  wire [3:0] bit_extender_4_out, Brancondition, flag_op_values_v3_v2_v1_v0, i_for_interrupt,
       multiplexer_7_out;
  wire [4:0] Flag_manipulations_new_cbcvzs_flags, load_store_flags_1_newcbcvzsflags,
       New_Flags_rstrf_or_alu_flags, NewIncOrDecFlags, NewShiftFlags, NewVSZCCBFlags, NormalOPFlags,
       RSTRF_restored_flags;
  wire [5:0] IncorDecBits;
  wire [6:0] keyboard_1_data, keyboard_2_data;
  wire [7:0] putchar_ord;
  wire [11:0] Interrupt;
  wire [15:0] adder_1_out, ALUResult, bit_extender_1_out, bit_extender_2_out, bit_extender_3_out,
       BranchingPC, Current_PC_t, DataFromKey1, DataFromKey2, hardware_i, IncOrDecResult, interrupt_op_code,
       interrupt_pc, multiplexer_13_out, multiplexer_16_out, multiplexer_21_out, NormalResultData,
       Register_File_out_10, Register_File_out_11, Register_File_out_14, Register_File_out_15,
       Register_File_out_16, Register_File_out_17, Register_File_out_18, Register_File_out_19,
       Register_File_out_20, Register_File_out_21, Register_File_out_22, Register_File_out_23,
       Register_File_out_24, Register_File_out_25, Register_File_out_26, Register_File_out_27, ResultData,
       rom_2_data, rom_3_data, rom_4_data, SetHigh_out_3, Shift_Inc_Or_Dec_Result;

  Operation_Control Operation_Control (
    .OpCode(out_8), .out_2({L_S_op, L_S, out_4[4]}), ._1_for_Halt__o_w_0(isHalt),
    .Destination_register_address_or_flag_op_v4(Brancondition),
    .Source_A_register_address_or_shift_operation_or_flag_operations(out_4[3:0]),
    .Source_B_register_address_or_flags_values_v3_v2(flag_op_values_v3_v2_v1_v0),
    .IncOrDecOperation({IncorDec_Operation[1], IncorDec}), .IncrementOrDecrementBits(IncorDecBits),
    .Values_For_SETLO_and_SETHIGH_or_bran_offset(out_5), .putchar_op(putchar_ord), .Interrupt(Interrupt));  // open: SaveOrRestores_flags
  assign bit_extender_1_out = {{8{out_5[7]}}, out_5};  // Bit_Extender bit_extender_1
  Multiplexer #(.width(16)) multiplexer_1 (
    .in0(out_15), .in1(IncOrDecResult), .out(Shift_Inc_Or_Dec_Result), .sel(IncorDec_Operation[1]));  // open: en
  Comparator #(.width(4)) comparator_1 (
    .a(4'b0000), .b({L_S_op, L_S, out_4[4]}), .eq(comparator_1_eq));  // open: gt, lt
  Comparator #(.width(4)) comparator_2 (
    .a({L_S_op, L_S, out_4[4]}), .b(4'b0001), .eq(RegisMode_relative));  // open: gt, lt
  Adder #(.width(16)) adder_1 (.a(Current_PC_t), .b(bit_extender_1_out), .out(adder_1_out));  // open: cin, cout
  Shift_Operations Shift_Operation (
    .Shift_Operation(out_4[2:0]), .A(out_7), .CBCVZSflags(CBCVZSFlags), .out_4(out_15),
    .NewCBCVZSflags(NewShiftFlags));
  Increment_Or_Decrement Increment_Or_Decrement (
    .in_1(IncorDec), .A(contents_of_Rd), .in_3(IncorDecBits), .CBCVZSflags(CBCVZSFlags),
    .out_5(IncOrDecResult), .NewCBCVZSflags(NewIncOrDecFlags));
  Multiplexer multiplexer_2 (.in0(1'b1), .in1(1'b0), .out(enabled_SaveOrRestore), .sel(and_1_out));  // open: en
  and and_1 (and_1_out, comparator_3_eq, comparator_4_eq, comparator_5_eq);
  Comparator #(.width(4)) comparator_3 (
    .a({L_S_op, L_S, out_4[4]}), .b(4'b0011), .eq(comparator_3_eq));  // open: gt, lt
  Comparator #(.width(4)) comparator_4 (.a(out_4[3:0]), .b(4'b0111), .eq(comparator_4_eq));  // open: gt, lt
  Comparator #(.width(4)) comparator_5 (
    .a(flag_op_values_v3_v2_v1_v0), .b(4'b1000), .eq(comparator_5_eq));  // open: gt, lt
  and and_2 (and_2_out, comparator_6_eq, comparator_7_eq);
  Comparator #(.width(4)) comparator_6 (
    .a({L_S_op, L_S, out_4[4]}), .b(4'b0011), .eq(comparator_6_eq));  // open: gt, lt
  Comparator #(.width(4)) comparator_7 (.a(out_4[3:0]), .b(4'b0110), .eq(comparator_7_eq));  // open: gt, lt
  or or_1 (IsBranOp, comparator_1_eq, RegisMode_relative);
  Multiplexer #(.width(16)) multiplexer_3 (
    .in0(adder_1_out), .in1(out_7), .out(BranchingPC), .sel(RegisMode_relative));  // open: en
  Multiplexer multiplexer_4 (.in0(1'b1), .in1(1'b0), .out(enabled_Flags_M), .sel(and_2_out));  // open: en
  Clock clock_1 (.out(Clock));
  ALU ALU (
    .OperationSelect({L_S_op[1], L_S, out_4[4]}), .A(out_6), .B(out_7), .CBCVZSflags(CBCVZSFlags),
    .Result_Data(ALUResult), .NewCBCVZSFlags(NewALUFlags), .enabled_register_file(enabled_register_file));
  Multiplexer #(.width(16)) multiplexer_5 (
    .in0(BranchingPC), .in1(out_7), .out(New_PC), .sel(IsCall_Return));  // open: en
  Multiplexer #(.width(5)) multiplexer_6 (
    .in0(NewShiftFlags), .in1(NewIncOrDecFlags), .out(out_14), .sel(IncorDec_Operation[1]));  // open: en
  Comparator #(.width(4)) comparator_8 (
    .a({L_S_op, L_S, out_4[4]}), .b(4'b0011), .eq(comparator_8_eq));  // open: gt, lt
  Comparator #(.width(4)) comparator_9 (.a(out_4[3:0]), .b(4'b0111), .eq(comparator_9_eq));  // open: gt, lt
  Comparator #(.width(4)) comparator_10 (
    .a(flag_op_values_v3_v2_v1_v0), .b(4'b1000), .eq(comparator_10_eq));  // open: gt, lt
  Flag_Manipulations Flag_manipulations (
    .Flag_op_and_v4(Brancondition), .v3__v2__v1__v0(flag_op_values_v3_v2_v1_v0),
    .CurrentCBCVZSflags(CBCVZSFlags), .New_CBCVZS_flags(Flag_manipulations_new_cbcvzs_flags));
  Multiplexer #(.width(4)) multiplexer_7 (
    .in0(Brancondition), .in1(out_4[3:0]), .out(multiplexer_7_out), .sel(keyInput));  // open: en
  not not_1 (not_1_out, IsBranOp);
  not not_2 (not_2_out, isStore);
  not not_3 (not_3_out, IsCall_Return);
  Multiplexer #(.select(4), .width(5), .disabled(0)) multiplexer_8 (
    .in0(CBCVZSFlags), .in1(CBCVZSFlags), .in2(CBCVZSFlags), .in3(out_14), .in4(CBCVZSFlags),
    .in5(CBCVZSFlags), .in6(CBCVZSFlags), .in7(CBCVZSFlags), .in8(NewALUFlags), .in9(NewALUFlags),
    .in10(NewALUFlags), .in11(NewALUFlags), .in12(NewALUFlags), .in13(NewALUFlags), .in14(CBCVZSFlags),
    .in15(CBCVZSFlags), .out(NewVSZCCBFlags), .sel({L_S_op, L_S, out_4[4]}));  // open: en
  Multiplexer #(.width(5)) multiplexer_9 (
    .in0(NewVSZCCBFlags), .in1(RSTRF_restored_flags), .out(New_Flags_rstrf_or_alu_flags), .sel(and_3_out));  // open: en
  RSTRF RSTRF (.Destination_Data_where_flags_are_stored(contents_of_Rd), .Restored_Flags(RSTRF_restored_flags));
  and and_3 (and_3_out, comparator_8_eq, comparator_9_eq, comparator_10_eq);
  Multiplexer #(.width(5)) multiplexer_10 (
    .in0(New_Flags_rstrf_or_alu_flags), .in1(Flag_manipulations_new_cbcvzs_flags), .out(NormalOPFlags),
    .sel(and_4_out));  // open: en
  and and_4 (and_4_out, comparator_11_eq, comparator_12_eq);
  Comparator #(.width(4)) comparator_11 (
    .a({L_S_op, L_S, out_4[4]}), .b(4'b0011), .eq(comparator_11_eq));  // open: gt, lt
  Comparator #(.width(4)) comparator_12 (.a(out_4[3:0]), .b(4'b0110), .eq(comparator_12_eq));  // open: gt, lt
  xor xor_1 (xor_1_out, CBCVZSFlags[0], CBCVZSFlags[2]);
  not not_4 (not_4_out, xor_1_out);
  or or_2 (or_2_out, xor_1_out, CBCVZSFlags[1]);
  not not_5 (not_5_out, CBCVZSFlags[3]);
  or or_3 (or_3_out, CBCVZSFlags[1], not_5_out);
  and and_5 (and_5_out, not_1_out, not_2_out, not_3_out);
  not not_6 (not_6_out, or_2_out);
  not not_7 (not_7_out, or_3_out);
  not not_8 (not_8_out, CBCVZSFlags[1]);
  not not_9 (not_9_out, CBCVZSFlags[3]);
  not not_10 (not_10_out, CBCVZSFlags[0]);
  not not_11 (not_11_out, CBCVZSFlags[2]);
  assign bit_extender_2_out = {{8{out_5[7]}}, out_5};  // Bit_Extender bit_extender_2
  SETHIGH SetHigh (.in_1(contents_of_Rd), .in_2(out_5), .out_3(SetHigh_out_3));
  not not_12 (not_12_out, IsBranOp);
  not not_13 (not_13_out, isStore);
  // Probe on Register_File_out_11
  // Probe on Register_File_out_14
  // Probe on Register_File_out_16
  // Probe on Register_File_out_18
  // Probe on Register_File_out_20
  // Probe on Register_File_out_22
  // Probe on Register_File_out_24
  // Probe on Register_File_out_26
  // Probe on Flags_out_5
  Flags Flags (
    .Clock(Clock), .enabled(and_5_out), .NewCBCVZSflags(out_11), .CBCVZSFlags(CBCVZSFlags),
    .out_5(Flags_out_5), .out_6(Flags_out_6), .out_7(Flags_out_7), .out_8(Flags_out_8), .out_9(Flags_out_9));
  // Probe on Flags_out_6
  // Probe on Flags_out_7
  // Probe on Flags_out_8
  // Probe on Flags_out_9
  and and_6 (and_6_out, IsBranOp, NeedToBran);
  not not_14 (not_14_out, isHalt);
  Multiplexer #(.select(4)) multiplexer_11 (
    .in0(1'b1), .in1(1'b0), .in2(xor_1_out), .in3(not_4_out), .in4(or_2_out), .in5(not_6_out),
    .in6(or_3_out), .in7(not_7_out), .in8(CBCVZSFlags[1]), .in9(not_8_out), .in10(CBCVZSFlags[3]),
    .in11(not_9_out), .in12(CBCVZSFlags[0]), .in13(not_10_out), .in14(CBCVZSFlags[2]), .in15(not_11_out),
    .out(NeedToBran), .sel(Brancondition));  // open: en
  // Probe on Register_File_out_10
  // Probe on Register_File_out_15
  // Probe on Register_File_out_17
  // Probe on Register_File_out_19
  // Probe on Register_File_out_21
  // Probe on Register_File_out_23
  // Probe on Register_File_out_25
  // Probe on Register_File_out_27
  Multiplexer #(.select(4), .width(16), .disabled(0)) multiplexer_12 (
    .in3(Shift_Inc_Or_Dec_Result), .in8(ALUResult), .in9(ALUResult), .in10(ALUResult), .in11(ALUResult),
    .in12(ALUResult), .in13(ALUResult), .in14(bit_extender_2_out), .in15(SetHigh_out_3), .out(out_12),
    .sel({L_S_op, L_S, out_4[4]}));  // open: in0, in1, in2, in4, in5, in6, in7, en
  and and_7 (and_7_out, enabled_SaveOrRestore, not_12_out, not_13_out, enabled_Flags_M);
  and and_8 (and_8_out, and_6_out, not_14_out);
  not not_15 (not_15_out, and_6_out);
  and and_9 (and_9_out, not_15_out, not_14_out);
  nor nor_1 (nor_1_out, IsRTI, ~or_4_out);  // NOR_Gate
  or or_4 (or_4_out, IsInterrupt, Interrupting);
  and and_10 (and_10_out, IsBranOp, NeedToBran);
  not not_16 (not_16_out, and_10_out);
  not not_17 (not_17_out, isHalt);
  or or_5 (or_5_out, Interrupting, IsInterrupt);
  or or_6 (enabled, and_7_out, keyboardEnabled, isLoad);
  Multiplexer #(.width(16)) multiplexer_13 (
    .in0({16{1'b0}}), .in1(New_PC), .out(multiplexer_13_out), .sel(and_11_out));  // open: en
  or or_7 (or_7_out, IsCall_Return, and_8_out);
  and and_11 (and_11_out, or_7_out, Interrupting);
  and and_12 (and_12_out, and_9_out, ~IsCall_Return);  // AND_Gate
  Register_File Register_File (
    .Read_Address_A(out_4[3:0]), .Read_Address_B(flag_op_values_v3_v2_v1_v0),
    .Write_Address(multiplexer_7_out), .Write_Data(ResultData), .clock(Clock), .enable(enabled),
    .out_9(out_6), .out_12(out_7), .out_13(contents_of_Rd), .out_11(Register_File_out_11),
    .out_14(Register_File_out_14), .out_16(Register_File_out_16), .out_18(Register_File_out_18),
    .out_20(Register_File_out_20), .out_22(Register_File_out_22), .out_24(Register_File_out_24),
    .out_26(Register_File_out_26), .out_27(Register_File_out_27), .out_25(Register_File_out_25),
    .out_23(Register_File_out_23), .out_21(Register_File_out_21), .out_19(Register_File_out_19),
    .out_17(Register_File_out_17), .out_15(Register_File_out_15), .out_10(Register_File_out_10),
    .Current_PC(Current_PC_t), .IsCall_Return(IsCall_Return));
  Register #(.width(1)) register_1 (.D(nor_1_out), .en(or_4_out), .Q(Interrupting), .clk(Clock));  // open: clr
  Register #(.width(4)) register_2 (
    .D(flag_op_values_v3_v2_v1_v0), .en(IsInterrupt), .Q(i_for_interrupt), .clk(Clock));  // open: clr
  or or_8 (or_8_out, Interrupting, IsInterrupt);
  not not_18 (not_18_out, or_8_out);
  or or_9 (or_9_out, IsCall_Return, and_13_out);
  and and_13 (and_13_out, and_10_out, not_17_out);
  and and_14 (and_14_out, not_16_out, not_17_out);
  and and_15 (and_15_out, and_14_out, ~IsCall_Return);  // AND_Gate
  // Probe on New_PC
  or or_10 (or_10_out, IsRTI, and_11_out);
  and and_16 (and_16_out, ~IsRTI, Interrupting);  // AND_Gate
  and and_17 (and_17_out, and_16_out, and_12_out);
  and and_18 (and_18_out, not_18_out, or_9_out);
  Counter #(.width(16), .max('hffff)) PC_register (
    .load(and_18_out), .D(New_PC), .count(and_19_out), .Q(Current_PC), .clk(Clock));  // open: carry, clr
  and and_19 (and_19_out, and_15_out, ~or_5_out);  // AND_Gate
  Counter #(.width(16), .max('hffff)) u_Interrupt_PC (
    .load(or_10_out), .D(multiplexer_13_out), .count(and_17_out), .Q(interrupt_pc), .clk(Clock));  // open: carry, clr
  assign bit_extender_3_out = {{11{1'b0}}, out_4};  // Bit_Extender bit_extender_3
  Comparator #(.width(3)) comparator_13 (.a({L_S_op, L_S}), .b(3'b010), .eq(isLoad));  // open: gt, lt
  Comparator comparator_14 (
    .a(8'h20), .b({L_S_op, L_S, out_4[4], Brancondition}), .eq(comparator_14_eq));  // open: gt, lt
  Comparator comparator_15 (
    .a({L_S_op, L_S, out_4[4], Brancondition}), .b(8'h21), .eq(comparator_15_eq));  // open: gt, lt
  Comparator #(.width(16)) comparator_16 (.a(16'h2300), .b(out_8), .eq(IsRTI));  // open: gt, lt
  ROM #(.addrWidth(16), .dataWidth(16)) rom_1 ();  // open: addr, data, sel
  RAM #(.addrWidth(16), .dataWidth(16), .bus("separate")) ram_1 (
    .addr(Memory_Address), .din(contents_of_Rd), .data(out_3), .str(isStore), .clk(Clock), .ld(isLoad));  // open: sel, clr
  Adder #(.width(16)) adder_2 (.a(out_7), .b(bit_extender_3_out), .out(Memory_Address));  // open: cin, cout
  Load_Store_flags load_store_flags_1 (
    .in_1(NormalResultData), .CurrentCBCVZSflags(CBCVZSFlags),
    .NewCBCVZSflags(load_store_flags_1_newcbcvzsflags));
  Comparator #(.width(12)) comparator_17 (.a(12'h220), .b(Interrupt), .eq(IsInterrupt));  // open: gt, lt
  ROM #(.addrWidth(16), .dataWidth(16)) rom_2 (.addr(Current_PC), .data(rom_2_data));  // open: sel
  Comparator #(.width(3)) comparator_18 (.a({L_S_op, L_S}), .b(3'b011), .eq(isStore));  // open: gt, lt
  Multiplexer #(.width(16)) multiplexer_14 (
    .in0(out_12), .in1(out_3), .out(NormalResultData), .sel(isLoad));  // open: en
  Multiplexer #(.width(5)) multiplexer_15 (
    .in0(NormalOPFlags), .in1(load_store_flags_1_newcbcvzsflags), .out(out_11), .sel(isLoad));  // open: en
  or or_11 (IsCall_Return, comparator_14_eq, comparator_15_eq);
  not not_19 (not_19_out, hardware_Interrupt);
  Multiplexer #(.width(16)) multiplexer_16 (
    .in0(hardware_i), .in1(rom_2_data), .out(multiplexer_16_out), .sel(not_19_out));  // open: en
  ROM #(.addrWidth(16), .dataWidth(16)) rom_3 (.addr(interrupt_pc), .data(rom_3_data));  // open: sel
  ROM #(.addrWidth(16), .dataWidth(16)) rom_4 (.addr(interrupt_pc), .data(rom_4_data));  // open: sel
  Multiplexer #(.select(2), .width(16)) multiplexer_17 (
    .in0(NormalResultData), .in1(NormalResultData), .in2(DataFromKey1), .in3(DataFromKey2), .out(ResultData),
    .sel({keyInput, flag_op_values_v3_v2_v1_v0[0]}));  // open: en
  Multiplexer #(.width(16)) multiplexer_18 (
    .in0(multiplexer_16_out), .in1(interrupt_op_code), .out(out_8), .sel(Interrupting));  // open: en
  Multiplexer #(.select(4), .width(16)) multiplexer_19 (
    .in0(rom_3_data), .in1(rom_4_data), .out(interrupt_op_code), .sel(i_for_interrupt));  // open: in2, in3, in4, in5, in6, in7, in8, in9, in10, in11, in12, in13, in14, in15, en
  Comparator comparator_19 (.a(8'h24), .b(putchar_ord), .eq(printToScreen));  // open: gt, lt
  xor xor_2 (xor_2_out, Interrupting, IsRTI);
  Multiplexer #(.width(16)) multiplexer_20 (
    .in0(Current_PC), .in1(interrupt_pc), .out(Current_PC_t), .sel(xor_2_out));  // open: en
  ROM rom_5 ();  // open: addr, data, sel
  not not_20 (not_20_out, flag_op_values_v3_v2_v1_v0[0]);
  TTY tty_1 (.data(out_6[6:0]), .clk(Clock), .we(and_20_out));  // open: clr
  and and_20 (and_20_out, not_20_out, printToScreen);
  TTY tty_2 (.data(out_6[6:0]), .clk(Clock), .we(and_21_out));  // open: clr
  and and_21 (and_21_out, flag_op_values_v3_v2_v1_v0[0], printToScreen);
  or or_12 (hardware_Interrupt, Key1Available, Key2Available);
  and and_22 (and_22_out, Key1Available, Key2Available);
  or or_13 (or_13_out, Key1Available, Key2Available);
  Multiplexer #(.select(4), .width(16)) multiplexer_21 (
    .in0(16'h2200), .in1(16'h2201), .out(multiplexer_21_out), .sel(bit_extender_4_out));  // open: in2, in3, in4, in5, in6, in7, in8, in9, in10, in11, in12, in13, in14, in15, en
  assign bit_extender_4_out = {{3{1'b0}}, and_22_out};  // Bit_Extender bit_extender_4
  Register #(.width(16)) register_3 (.D(multiplexer_21_out), .en(or_13_out), .Q(hardware_i), .clk(Clock));  // open: clr
  Comparator comparator_20 (.a(8'h25), .b(putchar_ord), .eq(keyInput));  // open: gt, lt
  not not_21 (not_21_out, flag_op_values_v3_v2_v1_v0[0]);
  Keyboard keyboard_1 (.clk(Clock), .re(and_23_out), .avail(Key1Available), .data(keyboard_1_data));  // open: clr
  and and_23 (and_23_out, not_21_out, keyInput);
  Keyboard keyboard_2 (.clk(Clock), .re(and_24_out), .avail(Key2Available), .data(keyboard_2_data));  // open: clr
  and and_24 (and_24_out, flag_op_values_v3_v2_v1_v0[0], keyInput);
  Multiplexer #(.select(2)) multiplexer_22 (
    .in0(1'b0), .in1(1'b0), .in2(Key1Available), .in3(Key2Available), .out(keyboardEnabled),
    .sel({keyInput, flag_op_values_v3_v2_v1_v0[0]}));  // open: en
  assign DataFromKey1 = {{9{1'b0}}, keyboard_1_data};  // Bit_Extender bit_extender_5
  assign DataFromKey2 = {{9{1'b0}}, keyboard_2_data};  // Bit_Extender bit_extender_6

  assign out_9 = contents_of_Rd;

  // Other names for the same wires on the sheet: Call_Return[3:0] = Brancondition;
  //   Destination_Source_Address[3:0] = Brancondition; flag_op_v4[3:0] = Brancondition; MemoryOff[4:0] = out_4;
  //   MemoryOp_l_s_o4[3:0] = {L_S_op, L_S, out_4[4]}; o4 = out_4[4]; Operation_Select[3:0] = {L_S_op, L_S, out_4[4]};
  //   S0 = out_4[4]; L_S_op[0] = L_S; S1 = L_S; S2 = L_S_op[1]; S3 = L_S_op[2];
  //   screenOrKeyOp = flag_op_values_v3_v2_v1_v0[0]; Source_B_Source_Address[3:0] = flag_op_values_v3_v2_v1_v0;
  //   A[15:0] = out_6; data_for_screen[6:0] = out_6[6:0]; B[15:0] = out_7; IncorDec_Operation[0] = IncorDec;
  //   the_7th_bit = IncorDec_Operation[1]; LoadResultData[15:0] = out_3; Memory_R_W_addr[15:0] = Memory_Address;
  //   o3_o2_o1_o0[3:0] = out_4[3:0]; SaveOrRestore_flag_operations[3:0] = out_4[3:0];
  //   Shift_operations[3:0] = out_4[3:0]; Source_A_Source_Address[3:0] = out_4[3:0]; NewFlags[4:0] = out_11;
  //   OpCode[15:0] = out_8; OPResultData[15:0] = out_12; Regular_PC[15:0] = Current_PC;
  //   SETdata[15:0] = contents_of_Rd; Shift_Inc_Or_Dec_Flags[4:0] = out_14; ShiftResult[15:0] = out_15;
  //   BranOffset[7:0] = out_5; Value_for_SETLO_and_SETHI[7:0] = out_5; CurrentS = CBCVZSFlags[0];
  //   VSZCCBFlags[4:0] = CBCVZSFlags; CurrentZ = CBCVZSFlags[1]; CurrentV = CBCVZSFlags[2]; CurrentC = CBCVZSFlags[3];
  //   CurrentCB = CBCVZSFlags[4]

  // Notes on the sheet:
  //   0000
  //   0001
  //   1 for register mode, 0 for relative branching
  //   Note: the tunnel VSZCCBflags is actually CBCVZS.
  //   0 if Shift operation, 1 if inc/dec operations
  //   0011
  //   0111
  //   1000
  //   0011
  //   0110
  //   0 if Shift operation, 1 if inc/dec operations
  //   BR
  //   BL
  //   BGE
  //   BLE
  //   010
  //   00100000
  //   00100001
  //   001000100000
  //   Memory RAM
  //   Program ROM
  //   contents of rom_1 (hex, n*v repeats v):
  //   3160 e4e8 f403 e5e8 f503 9cf0 e201 f200 ed3b fd00 20cd a010 eb13 fb00 180b 6105 3580 eb04 fb00 100b
  //   4104 a010 eb22 fb00 180b 9cf0 e201 f200 ed25 fd00 20cd 3480 eb13 fb00 100b eb38 fb00 100b 3f82 6d0e
  //   6c1e a020 eb46 fb00 180b 2410 eb4a fb00 100b 2411 eb4a fb00 100b 4d0e 4c1e 3fc2 21cd eb4e fb00 100b
  //   3f82 6d0e 6c1e a020 eb46 fb00 180b 2510 eb4a fb00 100b 2511 eb4a fb00 100b 4d0e 4c1e 3fc2 21cd
  //   011
  //   contents of rom_2 (hex, n*v repeats v):
  //   e3e8 f303 e4e8 f403 e501 f500 a656 eb06 fb00 100b 150*0 e101 f100 a212 eb02 fb00 100b
  //   contents of rom_3 (hex, n*v repeats v):
  //   6d00 6b10 9cf0 e200 f200 ed2d fd00 20cd 3068 b010 eb14 fb00 180b 9cf0 ed17 fd00 20cd eb02 fb00 100b
  //   eb2a fb00 100b 3f82 6d0e 6c1e a020 eb22 fb00 180b 2411 eb26 fb00 100b 2410 eb26 fb00 100b 4d0e 4c1e
  //   3fc2 21cd eb40 fb00 100b 3f82 6d0e 6c1e a020 eb38 fb00 180b 2511 eb3c fb00 100b 2510 eb3c fb00 100b
  //   4d0e 4c1e 3fc2 21cd 4d00 4b10 2300
  //   contents of rom_4 (hex, n*v repeats v):
  //   60 ffe8 3 ffe8 3 fff0 1
  //   00100100
  //   Screen 1
  //   Screen 2
  //   00100101
  //   keyboard 1
  //   keyboard 2
endmodule

module ALU (
  input  [2:0] OperationSelect,
  input  [15:0] A,
  input  [15:0] B,
  input  [4:0] CBCVZSflags,
  output [15:0] Result_Data,
  output [4:0] NewCBCVZSFlags,
  output enabled_register_file
);

  wire ACarryOut, and_2_out, and_3_out, and_4_out, AOverflow, arithmetic_unit_1_carry_out,
       Arithmetic_Unit_2_carry_out, Cin, comparator_2_eq, comparator_2_gt, comparator_4_eq, MCOut, MOverflow,
       not_1_out, not_2_out, not_3_out, not_4_out, not_5_out, not_6_out, not_7_out, SCarryOut, SOverflow;
  wire [14:0] M15Carryout;
  wire [15:0] A___B, A___B_t, A___B_t_t, A_and_B, A_or_B, A_xor_B, adder_1_out, bit_extender_1_out,
       bit_extender_2_out, MCarryOut, subtractor_1_out, subtractor_2_out, tunnel, xor_2_out;
  wire [31:0] bit_extender_3_out, bit_extender_4_out, bit_extender_5_out;

  assign A_and_B = A & B;  // AND_Gate and_1, 16 bits wide
  assign A_or_B = A | B;  // OR_Gate or_1, 16 bits wide
  assign A_xor_B = A ^ B;  // XOR_Gate xor_1, 16 bits wide
  Arithmetic_Unit arithmetic_unit_1 (
    .Cin(Cin), .S1(1'b0), .S0(1'b1), .A(A), .B(B), .Overflow(AOverflow),
    .Carry_out(arithmetic_unit_1_carry_out));  // open: out_6
  Arithmetic_Unit Arithmetic_Unit_2 (
    .Cin(Cin), .S1(1'b1), .S0(1'b0), .A(A), .B(B), .Overflow(SOverflow),
    .Carry_out(Arithmetic_Unit_2_carry_out));  // open: out_6
  Multiplier #(.width(15)) multiplier_1 (.a(A[14:0]), .b(B[14:0]), .cout(M15Carryout));  // open: out, cin
  Multiplier #(.width(16)) multiplier_2 (.a(A), .b(B), .out(tunnel), .cout(MCarryOut));  // open: cin
  not not_1 (not_1_out, CBCVZSflags[4]);
  and and_2 (and_2_out, not_1_out, CBCVZSflags[3]);
  Adder #(.width(16)) adder_1 (.a(A), .b(B), .out(adder_1_out));  // open: cin, cout
  Multiplexer #(.width(16)) multiplexer_1 (.in0(tunnel), .in1(MCarryOut), .out(A___B), .sel(and_3_out));  // open: en
  and and_3 (and_3_out, not_2_out, not_3_out, not_4_out, not_5_out, CBCVZSflags[0]);
  not not_2 (not_2_out, CBCVZSflags[4]);
  not not_3 (not_3_out, CBCVZSflags[3]);
  not not_4 (not_4_out, CBCVZSflags[2]);
  not not_5 (not_5_out, CBCVZSflags[1]);
  Multiplexer multiplexer_2 (.in0(CBCVZSflags[3]), .in1(1'b0), .out(Cin), .sel(CBCVZSflags[4]));  // open: en
  Comparator #(.width(16), .mode("unsigned")) comparator_1 (
    .a(A___B_t), .b({16{1'b1}}), .gt(ACarryOut));  // open: eq, lt
  assign bit_extender_1_out = {{15{1'b0}}, and_2_out};  // Bit_Extender bit_extender_1
  not not_6 (not_6_out, CBCVZSflags[4]);
  and and_4 (and_4_out, not_6_out, not_7_out);
  not not_7 (not_7_out, CBCVZSflags[3]);
  Subtractor #(.width(16)) subtractor_1 (.a(A), .b(B), .out(subtractor_1_out));  // open: bin, bout
  Comparator #(.width(16), .mode("unsigned")) comparator_2 (
    .a(A), .b(B), .gt(comparator_2_gt), .eq(comparator_2_eq));  // open: lt
  Adder #(.width(16)) adder_2 (.a(adder_1_out), .b(bit_extender_1_out), .out(A___B_t));  // open: cin, cout
  Multiplexer #(.select(3), .disabled(0)) multiplexer_3 (
    .in0(CBCVZSflags[2]), .in1(CBCVZSflags[2]), .in2(AOverflow), .in3(SOverflow), .in4(MOverflow),
    .in5(CBCVZSflags[2]), .in6(CBCVZSflags[2]), .in7(CBCVZSflags[2]), .out(NewCBCVZSFlags[2]),
    .sel(OperationSelect));  // open: en
  assign bit_extender_2_out = {{15{1'b0}}, and_4_out};  // Bit_Extender bit_extender_2
  Multiplexer multiplexer_4 (.in0(comparator_2_gt), .in1(1'b1), .out(SCarryOut), .sel(comparator_2_eq));  // open: en
  Subtractor #(.width(16)) subtractor_2 (
    .a(subtractor_1_out), .b(bit_extender_2_out), .out(subtractor_2_out));  // open: bin, bout
  Multiplexer #(.width(16)) multiplexer_5 (
    .in0(subtractor_2_out), .in1({16{1'b0}}), .out(A___B_t_t), .sel(comparator_2_eq));  // open: en
  Comparator #(.width(16), .mode("unsigned")) comparator_3 (.a(tunnel), .b({16{1'b1}}), .gt(MCOut));  // open: eq, lt
  nor nor_1 (NewCBCVZSFlags[1], Result_Data[0], Result_Data[1], Result_Data[2], Result_Data[3], Result_Data[4], Result_Data[5], Result_Data[6], Result_Data[7], Result_Data[8], Result_Data[9], Result_Data[10], Result_Data[11], Result_Data[12], Result_Data[13], Result_Data[14], NewCBCVZSFlags[0]);
  Multiplexer #(.select(4), .width(16), .disabled(0)) multiplexer_6 (
    .in0(A), .in1(A), .in2(A), .in3(A), .in4(A), .in5(A), .in6(A), .in7(A), .in8(A_and_B), .in9(A_or_B),
    .in10(A___B_t), .in11(A___B_t_t), .in12(A___B), .in13(A_xor_B), .in14(A), .in15(A),
    .out({NewCBCVZSFlags[0], Result_Data[14:0]}), .sel({1'b1, OperationSelect}));  // open: en
  assign bit_extender_3_out = {{16{A[15]}}, A};  // Bit_Extender bit_extender_3
  assign bit_extender_4_out = {{16{B[15]}}, B};  // Bit_Extender bit_extender_4
  assign bit_extender_5_out = {{16{A___B[15]}}, A___B};  // Bit_Extender bit_extender_5
  Multiplexer #(.select(3), .disabled(0)) multiplexer_7 (
    .in0(CBCVZSflags[3]), .in1(CBCVZSflags[3]), .in2(ACarryOut), .in3(SCarryOut), .in4(MCOut),
    .in5(CBCVZSflags[3]), .in6(CBCVZSflags[3]), .in7(CBCVZSflags[3]), .out(NewCBCVZSFlags[3]),
    .sel(OperationSelect));  // open: en
  assign xor_2_out = bit_extender_3_out[31:16] ^ bit_extender_4_out[31:16];  // XOR_Gate xor_2, 16 bits wide
  Comparator #(.width(16)) comparator_4 (
    .a(xor_2_out), .b(bit_extender_5_out[31:16]), .eq(comparator_4_eq));  // open: gt, lt
  not not_8 (MOverflow, comparator_4_eq);

  assign enabled_register_file = 1'b1;
  assign NewCBCVZSFlags[4] = CBCVZSflags[4];
  assign Result_Data[15] = NewCBCVZSFlags[0];

  // Other names for the same wires on the sheet: S0 = OperationSelect[0]; S1 = OperationSelect[1];
  //   S2 = OperationSelect[2]; CurrentS = CBCVZSflags[0]; CurrentZ = CBCVZSflags[1]; CurrentV = CBCVZSflags[2];
  //   CurrentC = CBCVZSflags[3]; Z = NewCBCVZSFlags[1]; Overflow = NewCBCVZSFlags[2]; CarryOut = NewCBCVZSFlags[3];
  //   CurrentCB = CBCVZSflags[4]; ResultData[15:0] = {NewCBCVZSFlags[0], Result_Data[14:0]}; NewS = NewCBCVZSFlags[0]

  // Notes on the sheet:
  //   Inputs
  //   outputs
endmodule

module Arithmetic_Unit (
  input  Cin,
  input  S1,
  input  S0,
  input  [15:0] A,
  input  [15:0] B,
  output [15:0] out_6,
  output Overflow,
  output Carry_out
);

  wire adder_1_cout, adder_2_cout, adder_3_cout, adder_4_cout, adder_5_cout, adder_6_cout, adder_7_cout,
       adder_8_cout, adder_9_cout, adder_10_cout, adder_11_cout, adder_12_cout, adder_13_cout, adder_14_cout,
       adder_15_cout, and_1_out, and_2_out, and_3_out, and_4_out, and_5_out, and_6_out, and_7_out, and_8_out,
       and_9_out, and_10_out, and_11_out, and_12_out, and_13_out, and_14_out, and_15_out, and_16_out,
       and_17_out, and_18_out, and_19_out, and_20_out, and_21_out, and_22_out, and_23_out, and_24_out,
       and_25_out, and_26_out, and_27_out, and_28_out, and_29_out, and_30_out, and_31_out, and_32_out,
       not_1_out, not_2_out, not_3_out, not_4_out, not_5_out, not_6_out, not_7_out, not_8_out, not_9_out,
       not_10_out, not_11_out, not_12_out, not_13_out, not_14_out, not_15_out, not_16_out, or_1_out,
       or_2_out, or_3_out, or_4_out, or_5_out, or_6_out, or_7_out, or_8_out, or_9_out, or_10_out, or_11_out,
       or_12_out, or_13_out, or_14_out, or_15_out, or_16_out;

  not not_1 (not_1_out, B[0]);
  not not_2 (not_2_out, B[1]);
  not not_3 (not_3_out, B[2]);
  not not_4 (not_4_out, B[3]);
  not not_5 (not_5_out, B[4]);
  not not_6 (not_6_out, B[5]);
  not not_7 (not_7_out, B[6]);
  not not_8 (not_8_out, B[7]);
  not not_9 (not_9_out, B[8]);
  not not_10 (not_10_out, B[9]);
  not not_11 (not_11_out, B[10]);
  not not_12 (not_12_out, B[11]);
  not not_13 (not_13_out, B[12]);
  not not_14 (not_14_out, B[13]);
  not not_15 (not_15_out, B[14]);
  not not_16 (not_16_out, B[15]);
  and and_1 (and_1_out, S0, B[0]);
  and and_2 (and_2_out, not_1_out, S1);
  and and_3 (and_3_out, S0, B[1]);
  and and_4 (and_4_out, not_2_out, S1);
  and and_5 (and_5_out, S0, B[2]);
  and and_6 (and_6_out, not_3_out, S1);
  and and_7 (and_7_out, S0, B[3]);
  and and_8 (and_8_out, not_4_out, S1);
  and and_9 (and_9_out, S0, B[4]);
  and and_10 (and_10_out, not_5_out, S1);
  and and_11 (and_11_out, S0, B[5]);
  and and_12 (and_12_out, not_6_out, S1);
  and and_13 (and_13_out, S0, B[6]);
  and and_14 (and_14_out, not_7_out, S1);
  and and_15 (and_15_out, S0, B[7]);
  and and_16 (and_16_out, not_8_out, S1);
  and and_17 (and_17_out, S0, B[8]);
  and and_18 (and_18_out, not_9_out, S1);
  and and_19 (and_19_out, S0, B[9]);
  and and_20 (and_20_out, not_10_out, S1);
  and and_21 (and_21_out, S0, B[10]);
  and and_22 (and_22_out, not_11_out, S1);
  and and_23 (and_23_out, S0, B[11]);
  and and_24 (and_24_out, not_12_out, S1);
  and and_25 (and_25_out, S0, B[12]);
  and and_26 (and_26_out, not_13_out, S1);
  and and_27 (and_27_out, S0, B[13]);
  and and_28 (and_28_out, not_14_out, S1);
  and and_29 (and_29_out, S0, B[14]);
  and and_30 (and_30_out, not_15_out, S1);
  and and_31 (and_31_out, S0, B[15]);
  and and_32 (and_32_out, not_16_out, S1);
  or or_1 (or_1_out, and_1_out, and_2_out);
  or or_2 (or_2_out, and_3_out, and_4_out);
  or or_3 (or_3_out, and_5_out, and_6_out);
  or or_4 (or_4_out, and_7_out, and_8_out);
  or or_5 (or_5_out, and_9_out, and_10_out);
  or or_6 (or_6_out, and_11_out, and_12_out);
  or or_7 (or_7_out, and_13_out, and_14_out);
  or or_8 (or_8_out, and_15_out, and_16_out);
  or or_9 (or_9_out, and_17_out, and_18_out);
  or or_10 (or_10_out, and_19_out, and_20_out);
  or or_11 (or_11_out, and_21_out, and_22_out);
  or or_12 (or_12_out, and_23_out, and_24_out);
  or or_13 (or_13_out, and_25_out, and_26_out);
  or or_14 (or_14_out, and_27_out, and_28_out);
  or or_15 (or_15_out, and_29_out, and_30_out);
  or or_16 (or_16_out, and_31_out, and_32_out);
  Adder #(.width(1)) adder_1 (.a(A[0]), .b(or_1_out), .out(out_6[0]), .cin(Cin), .cout(adder_1_cout));
  Adder #(.width(1)) adder_2 (.a(A[1]), .b(or_2_out), .out(out_6[1]), .cin(adder_1_cout), .cout(adder_2_cout));
  Adder #(.width(1)) adder_3 (.a(A[2]), .b(or_3_out), .out(out_6[2]), .cin(adder_2_cout), .cout(adder_3_cout));
  Adder #(.width(1)) adder_4 (.a(A[3]), .b(or_4_out), .out(out_6[3]), .cin(adder_3_cout), .cout(adder_4_cout));
  Adder #(.width(1)) adder_5 (.a(A[4]), .b(or_5_out), .out(out_6[4]), .cin(adder_4_cout), .cout(adder_5_cout));
  Adder #(.width(1)) adder_6 (.a(A[5]), .b(or_6_out), .out(out_6[5]), .cin(adder_5_cout), .cout(adder_6_cout));
  Adder #(.width(1)) adder_7 (.a(A[6]), .b(or_7_out), .out(out_6[6]), .cin(adder_6_cout), .cout(adder_7_cout));
  Adder #(.width(1)) adder_8 (.a(A[7]), .b(or_8_out), .out(out_6[7]), .cin(adder_7_cout), .cout(adder_8_cout));
  Adder #(.width(1)) adder_9 (.a(A[8]), .b(or_9_out), .out(out_6[8]), .cin(adder_8_cout), .cout(adder_9_cout));
  Adder #(.width(1)) adder_10 (.a(A[9]), .b(or_10_out), .out(out_6[9]), .cin(adder_9_cout), .cout(adder_10_cout));
  Adder #(.width(1)) adder_11 (.a(A[10]), .b(or_11_out), .out(out_6[10]), .cin(adder_10_cout), .cout(adder_11_cout));
  Adder #(.width(1)) adder_12 (.a(A[11]), .b(or_12_out), .out(out_6[11]), .cin(adder_11_cout), .cout(adder_12_cout));
  Adder #(.width(1)) adder_13 (.a(A[12]), .b(or_13_out), .out(out_6[12]), .cin(adder_12_cout), .cout(adder_13_cout));
  Adder #(.width(1)) adder_14 (.a(A[13]), .b(or_14_out), .out(out_6[13]), .cin(adder_13_cout), .cout(adder_14_cout));
  Adder #(.width(1)) adder_15 (.a(A[14]), .b(or_15_out), .out(out_6[14]), .cin(adder_14_cout), .cout(adder_15_cout));
  Adder #(.width(1)) adder_16 (.a(A[15]), .b(or_16_out), .out(out_6[15]), .cin(adder_15_cout), .cout(Carry_out));
  xor xor_1 (Overflow, adder_15_cout, Carry_out);

  // Other names for the same wires on the sheet: Cout = Carry_out; O0 = out_6[0]; Output[15:0] = out_6; O1 = out_6[1];
  //   O2 = out_6[2]; O3 = out_6[3]; O4 = out_6[4]; O5 = out_6[5]; O6 = out_6[6]; O7 = out_6[7]; O8 = out_6[8];
  //   O9 = out_6[9]; O10 = out_6[10]; O11 = out_6[11]; O12 = out_6[12]; O13 = out_6[13]; O14 = out_6[14];
  //   O15 = out_6[15]; V = Overflow
endmodule

module Logic_Unit (
  input  S0,
  input  S1,
  input  [15:0] A,
  input  [15:0] B,
  output [15:0] out_5
);

  wire [15:0] and_1_out, not_1_out, or_1_out, xor_1_out;

  assign and_1_out = A & B;  // AND_Gate and_1, 16 bits wide
  assign or_1_out = A | B;  // OR_Gate or_1, 16 bits wide
  assign xor_1_out = A ^ B;  // XOR_Gate xor_1, 16 bits wide
  assign not_1_out = ~A;  // NOT_Gate not_1, 16 bits wide
  Multiplexer #(.select(2), .width(16)) multiplexer_1 (
    .in0(and_1_out), .in1(or_1_out), .in2(xor_1_out), .in3(not_1_out), .out(out_5), .sel({S1, S0}));  // open: en

  // Other names for the same wires on the sheet: Output[15:0] = out_5; Select_Bits[1:0] = {S1, S0}
endmodule

module Shift_Right_unit (
  input  in_1,
  input  [15:0] A,
  input  S1,
  input  S0,
  output [15:0] out_5
);

  wire [0:0] shifter_3_out;
  wire [15:0] ArithmeticShiftRight, LogicalShiftRight, Rotate_Right, RotateRightWithCarry;

  Shifter #(.width(16), .shift("lr")) shifter_1 (.in(A), .\dist (4'b0001), .out(LogicalShiftRight));
  Shifter #(.width(16), .shift("rr")) shifter_2 (.in(A), .\dist (4'b0001), .out(Rotate_Right));
  Shifter #(.width(17), .shift("rr")) shifter_3 (
    .in({A, in_1}), .\dist (5'b00001), .out({RotateRightWithCarry, shifter_3_out[0]}));
  Shifter #(.width(16), .shift("ar")) shifter_4 (.in(A), .\dist (4'b0001), .out(ArithmeticShiftRight));
  Multiplexer #(.select(2), .width(16)) multiplexer_1 (
    .in0(LogicalShiftRight), .in1(Rotate_Right), .in2(RotateRightWithCarry), .in3(ArithmeticShiftRight),
    .out(out_5), .sel({S1, S0}));  // open: en

  // Other names for the same wires on the sheet: AWithCarry[16:0] = {A, in_1}; Carry = in_1;
  //   ShiftResult[15:0] = out_5
endmodule

module Operation_Control (
  input  [15:0] OpCode,
  output [3:0] out_2,
  output _1_for_Halt__o_w_0,
  output [3:0] Destination_register_address_or_flag_op_v4,
  output [3:0] Source_A_register_address_or_shift_operation_or_flag_operations,
  output [3:0] Source_B_register_address_or_flags_values_v3_v2,
  output [1:0] IncOrDecOperation,
  output [5:0] IncrementOrDecrementBits,
  output [7:0] Values_For_SETLO_and_SETHIGH_or_bran_offset,
  output SaveOrRestores_flags,
  output [7:0] putchar_op,
  output [11:0] Interrupt
);

  nor nor_1 (_1_for_Halt__o_w_0, OpCode[0], OpCode[1], OpCode[2], OpCode[3], OpCode[4], OpCode[5], OpCode[6], OpCode[7], OpCode[8], OpCode[9], OpCode[10], OpCode[11], OpCode[12], OpCode[13], OpCode[14], OpCode[15]);

  assign Destination_register_address_or_flag_op_v4 = OpCode[11:8];
  assign IncOrDecOperation = OpCode[7:6];
  assign IncrementOrDecrementBits = OpCode[5:0];
  assign Interrupt = OpCode[15:4];
  assign out_2 = OpCode[15:12];
  assign putchar_op = OpCode[15:8];
  assign SaveOrRestores_flags = OpCode[3];
  assign Source_A_register_address_or_shift_operation_or_flag_operations = OpCode[7:4];
  assign Values_For_SETLO_and_SETHIGH_or_bran_offset = OpCode[7:0];

  // Other names for the same wires on the sheet: BSourceAddr_t[3:0] = Source_B_register_address_or_flags_values_v3_v2;
  //   BSourceAddr[3:0] = OpCode[3:0]; SETValue[7:0] = OpCode[7:0]; SaveFlags_or_Restore = OpCode[3];
  //   ASourceAddr[3:0] = OpCode[7:4]; IncOrDec[1:0] = OpCode[7:6]; DestinationAddr[3:0] = OpCode[11:8];
  //   putchar_ord[7:0] = OpCode[15:8]; OperationSelect[3:0] = OpCode[15:12]; IsHalt = _1_for_Halt__o_w_0
endmodule

module Shift_Left_unit (
  input  in_1,
  input  [15:0] A,
  input  S1,
  input  S0,
  output [15:0] out_5
);

  wire [0:0] shifter_3_out;
  wire [15:0] ArithmeticShiftLeft, LogicalShiftLeft, Rotate_Left, RotateLeftWithCarry;

  Shifter #(.width(16)) shifter_1 (.in(A), .\dist (4'b0001), .out(LogicalShiftLeft));
  Shifter #(.width(16), .shift("rl")) shifter_2 (.in(A), .\dist (4'b0001), .out(Rotate_Left));
  Shifter #(.width(17), .shift("rl")) shifter_3 (
    .in({A, in_1}), .\dist (5'b00001), .out({RotateLeftWithCarry, shifter_3_out[0]}));
  Shifter #(.width(16)) shifter_4 (.in(A), .\dist (4'b0001), .out(ArithmeticShiftLeft));
  Multiplexer #(.select(2), .width(16)) multiplexer_1 (
    .in0(LogicalShiftLeft), .in1(Rotate_Left), .in2(RotateLeftWithCarry), .in3(ArithmeticShiftLeft),
    .out(out_5), .sel({S1, S0}));  // open: en

  // Other names for the same wires on the sheet: AWithCarry[16:0] = {A, in_1}; Carry = in_1;
  //   ShiftResult[15:0] = out_5
endmodule

module Flags (
  input  Clock,
  input  enabled,
  input  [4:0] NewCBCVZSflags,
  output [4:0] CBCVZSFlags,
  output out_5,
  output out_6,
  output out_7,
  output out_8,
  output out_9
);

  D_Flip_Flop CB (.clk(Clock), .D(NewCBCVZSflags[4]), .Q(CBCVZSFlags[4]), .en(enabled));  // open: Qn, preset, reset
  D_Flip_Flop C (.clk(Clock), .D(NewCBCVZSflags[3]), .Q(CBCVZSFlags[3]), .en(enabled));  // open: Qn, preset, reset
  D_Flip_Flop V (.clk(Clock), .D(NewCBCVZSflags[2]), .Q(CBCVZSFlags[2]), .en(enabled));  // open: Qn, preset, reset
  D_Flip_Flop Z (.clk(Clock), .D(NewCBCVZSflags[1]), .Q(CBCVZSFlags[1]), .en(enabled));  // open: Qn, preset, reset
  D_Flip_Flop S (.clk(Clock), .D(NewCBCVZSflags[0]), .Q(CBCVZSFlags[0]), .en(enabled));  // open: Qn, preset, reset

  assign out_5 = CBCVZSFlags[4];
  assign out_6 = CBCVZSFlags[3];
  assign out_7 = CBCVZSFlags[2];
  assign out_8 = CBCVZSFlags[1];
  assign out_9 = CBCVZSFlags[0];

  // Other names for the same wires on the sheet: S = CBCVZSFlags[0]; Z = CBCVZSFlags[1]; V = CBCVZSFlags[2];
  //   C = CBCVZSFlags[3]; CB = CBCVZSFlags[4]; enable = enabled; newS = NewCBCVZSflags[0]; newZ = NewCBCVZSflags[1];
  //   newV = NewCBCVZSflags[2]; newC = NewCBCVZSflags[3]; newCB = NewCBCVZSflags[4]
endmodule

module Shift_Operations (
  input  [2:0] Shift_Operation,
  input  [15:0] A,
  input  [4:0] CBCVZSflags,
  output [15:0] out_4,
  output [4:0] NewCBCVZSflags
);

  wire ASL_Overflow, ASLCarry, comparator_1_eq, comparator_2_eq, LeftShiftCarry, LRCarry, nor_1_out,
       not_1_out, not_2_out, RightShiftCarry, RLCarry, RRCarry;
  wire [0:0] AWithCarry;
  wire [15:0] ASL_Result, ASR_Result, bit_extender_1_out, LogicalShiftRightWithCarry, LSL8_Result,
       LSL_Result, LSR8_Result, LSR_Result, RotateLeftWithCarry, RotateRightWithCarry, xor_1_out;
  wire [31:0] bit_extender_2_out, bit_extender_3_out, bit_extender_4_out, bit_extender_5_out;

  not not_1 (not_1_out, CBCVZSflags[4]);
  and and_1 (AWithCarry[0], not_1_out, CBCVZSflags[3]);
  Shifter #(.width(17), .shift("rl")) shifter_1 (
    .in({A, AWithCarry[0]}), .\dist (5'b00001), .out({RotateLeftWithCarry, RLCarry}));
  Shifter #(.width(17), .shift("rr")) shifter_2 (
    .in({A, AWithCarry[0]}), .\dist (5'b00001), .out({RotateRightWithCarry, RRCarry}));
  Shifter #(.width(16)) shifter_3 (.in(A), .\dist (4'b1000), .out(LSL8_Result));
  Shifter #(.width(16), .shift("lr")) shifter_4 (.in(A), .\dist (4'b1000), .out(LSR8_Result));
  Shifter #(.width(16), .shift("ar")) shifter_5 (.in(A), .\dist (4'b0001), .out(ASR_Result));
  assign bit_extender_1_out = {{11{1'b0}}, CBCVZSflags};  // Bit_Extender bit_extender_1
  Shifter #(.width(17)) shifter_6 (.in({A, AWithCarry[0]}), .\dist (5'b00001), .out({ASL_Result, ASLCarry}));
  Shifter #(.width(17), .shift("lr")) shifter_7 (
    .in({A, AWithCarry[0]}), .\dist (5'b00001), .out({LogicalShiftRightWithCarry, LRCarry}));
  Multiplexer #(.select(3), .width(16)) multiplexer_1 (
    .in0(LSL_Result), .in1(LSR_Result), .in2(LSL8_Result), .in3(LSR8_Result), .in4(ASL_Result),
    .in5(ASR_Result), .in6(bit_extender_1_out), .in7(bit_extender_1_out), .out(out_4), .sel(Shift_Operation));  // open: en
  assign bit_extender_2_out = {{16{1'b0}}, ASL_Result};  // Bit_Extender bit_extender_2
  assign bit_extender_3_out = {{16{ASL_Result[15]}}, ASL_Result};  // Bit_Extender bit_extender_3
  Multiplexer #(.select(3)) multiplexer_2 (
    .in0(CBCVZSflags[2]), .in1(CBCVZSflags[2]), .in2(CBCVZSflags[2]), .in3(CBCVZSflags[2]),
    .in4(ASL_Overflow), .in5(CBCVZSflags[2]), .in6(CBCVZSflags[2]), .in7(CBCVZSflags[2]),
    .out(NewCBCVZSflags[2]), .sel(Shift_Operation));  // open: en
  Multiplexer #(.width(16)) multiplexer_3 (
    .in0(RotateLeftWithCarry), .in1(ASL_Result), .out(LSL_Result), .sel(CBCVZSflags[4]));  // open: en
  Multiplexer #(.width(16)) multiplexer_4 (
    .in0(RotateRightWithCarry), .in1(LogicalShiftRightWithCarry), .out(LSR_Result), .sel(CBCVZSflags[4]));  // open: en
  Comparator #(.width(32)) comparator_1 (
    .a(bit_extender_2_out), .b(bit_extender_3_out), .eq(comparator_1_eq));  // open: gt, lt
  not not_2 (not_2_out, comparator_1_eq);
  assign bit_extender_4_out = {{16{A[15]}}, A};  // Bit_Extender bit_extender_4
  Multiplexer #(.select(3)) multiplexer_5 (
    .in0(out_4[15]), .in1(out_4[15]), .in2(out_4[15]), .in3(out_4[15]), .in4(out_4[15]), .in5(out_4[15]),
    .in6(out_4[15]), .in7(CBCVZSflags[0]), .out(NewCBCVZSflags[0]), .sel(Shift_Operation));  // open: en
  assign bit_extender_5_out = {{16{ASL_Result[15]}}, ASL_Result};  // Bit_Extender bit_extender_5
  assign xor_1_out = bit_extender_4_out[31:16] ^ bit_extender_4_out[31:16];  // XOR_Gate xor_1, 16 bits wide
  nor nor_1 (nor_1_out, out_4[0], out_4[1], out_4[2], out_4[3], out_4[4], out_4[5], out_4[6], out_4[7], out_4[8], out_4[9], out_4[10], out_4[11], out_4[12], out_4[13], out_4[14], out_4[15]);
  Multiplexer multiplexer_6 (.in0(RLCarry), .in1(ASLCarry), .out(LeftShiftCarry), .sel(CBCVZSflags[4]));  // open: en
  Multiplexer multiplexer_7 (.in0(RRCarry), .in1(LRCarry), .out(RightShiftCarry), .sel(CBCVZSflags[4]));  // open: en
  Comparator #(.width(16)) comparator_2 (
    .a(xor_1_out), .b(bit_extender_5_out[31:16]), .eq(comparator_2_eq));  // open: gt, lt
  not not_3 (ASL_Overflow, comparator_2_eq);
  Multiplexer #(.select(3)) multiplexer_8 (
    .in0(LeftShiftCarry), .in1(RightShiftCarry), .in2(CBCVZSflags[3]), .in3(CBCVZSflags[3]), .in4(ASLCarry),
    .in5(A[0]), .in6(CBCVZSflags[3]), .in7(CBCVZSflags[3]), .out(NewCBCVZSflags[3]), .sel(Shift_Operation));  // open: en
  Multiplexer #(.select(3)) multiplexer_9 (
    .in0(nor_1_out), .in1(nor_1_out), .in2(nor_1_out), .in3(nor_1_out), .in4(nor_1_out), .in5(nor_1_out),
    .in6(nor_1_out), .in7(CBCVZSflags[1]), .out(NewCBCVZSflags[1]), .sel(Shift_Operation));  // open: en

  assign NewCBCVZSflags[4] = CBCVZSflags[4];

  // Other names for the same wires on the sheet: LLCarry = ASLCarry; LogicalShiftLeftWithCarry[15:0] = ASL_Result;
  //   ASRCarry = A[0]; AWithCarry[16:1] = A; CurrentS = CBCVZSflags[0]; CurrentZ = CBCVZSflags[1];
  //   CurrentV = CBCVZSflags[2]; CurrentC = CBCVZSflags[3]; NewS = NewCBCVZSflags[0]; NewZ = NewCBCVZSflags[1];
  //   NewV = NewCBCVZSflags[2]; NewC = NewCBCVZSflags[3]; CurrentCB = CBCVZSflags[4]; Shift_Result[15:0] = out_4
endmodule

module Increment_Or_Decrement (
  input  in_1,
  input  [15:0] A,
  input  [5:0] in_3,
  input  [4:0] CBCVZSflags,
  output [15:0] out_5,
  output [4:0] NewCBCVZSflags
);

  wire comparator_1_eq, comparator_1_gt, DecOverflow, Decrement_carry_out, IncOverflow, Increment_carry_out,
       NewAC, NewSC, subtractor_1_bout;
  wire [5:0] adder_1_out;
  wire [15:0] Dec, Inc, IncOrDec_1, subtractor_2_out;

  Adder #(.width(6)) adder_1 (.a(in_3), .b(6'b000001), .out(adder_1_out));  // open: cin, cout
  assign IncOrDec_1 = {{10{1'b0}}, adder_1_out};  // Bit_Extender bit_extender_1
  Adder #(.width(16)) adder_2 (.a(A), .b(IncOrDec_1), .out(Inc), .cout(NewAC));  // open: cin
  Subtractor #(.width(16)) subtractor_1 (.a(A), .b(IncOrDec_1), .bout(subtractor_1_bout));  // open: out, bin
  Subtractor #(.width(16)) subtractor_2 (.a(A), .b(IncOrDec_1), .out(subtractor_2_out));  // open: bin, bout
  Comparator #(.width(16), .mode("unsigned")) comparator_1 (
    .a(A), .b(IncOrDec_1), .gt(comparator_1_gt), .eq(comparator_1_eq));  // open: lt
  Multiplexer multiplexer_1 (.in0(comparator_1_gt), .in1(1'b1), .out(NewSC), .sel(comparator_1_eq));  // open: en
  Multiplexer #(.width(16)) multiplexer_2 (
    .in0(subtractor_2_out), .in1({16{1'b0}}), .out(Dec), .sel(comparator_1_eq));  // open: en
  Multiplexer #(.width(16)) multiplexer_3 (
    .in0(Inc), .in1(Dec), .out({NewCBCVZSflags[0], out_5[14:0]}), .sel(in_1));  // open: en
  Multiplexer multiplexer_4 (.in0(NewAC), .in1(NewSC), .out(NewCBCVZSflags[3]), .sel(in_1));  // open: en
  nor nor_1 (NewCBCVZSflags[1], out_5[0], out_5[1], out_5[2], out_5[3], out_5[4], out_5[5], out_5[6], out_5[7], out_5[8], out_5[9], out_5[10], out_5[11], out_5[12], out_5[13], out_5[14], NewCBCVZSflags[0]);
  Arithmetic_Unit Increment (
    .Cin(1'b1), .S1(1'b0), .S0(1'b1), .A(A), .B(IncOrDec_1), .Overflow(IncOverflow),
    .Carry_out(Increment_carry_out));  // open: out_6
  Arithmetic_Unit Decrement (
    .Cin(1'b1), .S1(1'b1), .S0(1'b0), .A(A), .B(IncOrDec_1), .Overflow(DecOverflow),
    .Carry_out(Decrement_carry_out));  // open: out_6
  Multiplexer multiplexer_5 (.in0(IncOverflow), .in1(DecOverflow), .out(NewCBCVZSflags[2]), .sel(in_1));  // open: en

  assign NewCBCVZSflags[4] = CBCVZSflags[4];
  assign out_5[15] = NewCBCVZSflags[0];

  // Other names for the same wires on the sheet: CurrentS = CBCVZSflags[0]; CurrentZ = CBCVZSflags[1];
  //   CurrentV = CBCVZSflags[2]; CurrentC = CBCVZSflags[3]; IncOrDec = in_1; IncOrDec_Bits[5:0] = in_3;
  //   NewZ = NewCBCVZSflags[1]; NewV = NewCBCVZSflags[2]; NewC = NewCBCVZSflags[3]; CurrentCB = CBCVZSflags[4];
  //   Result[15:0] = {NewCBCVZSflags[0], out_5[14:0]}; NewS = NewCBCVZSflags[0]
endmodule

module SETHIGH (
  input  [15:0] in_1,
  input  [7:0] in_2,
  output [15:0] out_3
);


  assign out_3 = {in_2, in_1[7:0]};

  // Other names for the same wires on the sheet: A[15:0] = in_1; Result[15:0] = {in_2, in_1[7:0]}; value[7:0] = in_2
endmodule

module Register_File (
  input  [3:0] Read_Address_A,
  input  [3:0] Read_Address_B,
  input  [3:0] Write_Address,
  input  [15:0] Write_Data,
  input  clock,
  input  enable,
  input  [15:0] Current_PC,
  input  IsCall_Return,
  output [15:0] out_9,
  output [15:0] out_10,
  output [15:0] out_11,
  output [15:0] out_12,
  output [15:0] out_13,
  output [15:0] out_14,
  output [15:0] out_15,
  output [15:0] out_16,
  output [15:0] out_17,
  output [15:0] out_18,
  output [15:0] out_19,
  output [15:0] out_20,
  output [15:0] out_21,
  output [15:0] out_22,
  output [15:0] out_23,
  output [15:0] out_24,
  output [15:0] out_25,
  output [15:0] out_26,
  output [15:0] out_27
);

  wire and_1_out, and_2_out, and_3_out, and_4_out, and_5_out, and_6_out, and_7_out, and_8_out, and_9_out,
       and_10_out, and_11_out, and_12_out, and_13_out, and_14_out, and_15_out, and_16_out, and_17_out,
       or_1_out, or_2_out, RAAw0, RAAw1, RAAw2, RAAw3, RAAw4, RAAw5, RAAw6, RAAw7, RAAw8, RAAw9, RAAw10,
       RAAw11, RAAw12, RAAw13, RAAw14, RAAw15, w0, w1, w2, w3, w4, w5, w6, w7, w8, w9, w10, w11, w12, w13,
       w14, w15;
  wire [3:0] WA;
  wire [15:0] adder_1_out, FP, multiplexer_6_out, New_FP, New_RDA, WD;

  Adder #(.width(16)) adder_1 (.a(Current_PC), .b(16'h1), .out(adder_1_out));  // open: cin, cout
  Demultiplexer #(.select(4), .disabled(0)) demultiplexer_1 (
    .out0(w0), .out1(w1), .out2(w2), .out3(w3), .out4(w4), .out5(w5), .out6(w6), .out7(w7), .out8(w8),
    .out9(w9), .out10(w10), .out11(w11), .out12(w12), .out13(w13), .out14(w14), .out15(w15), .in(1'b1),
    .sel(WA), .en(enable));
  Demultiplexer #(.select(4), .disabled(0)) demultiplexer_2 (
    .out0(RAAw0), .out1(RAAw1), .out2(RAAw2), .out3(RAAw3), .out4(RAAw4), .out5(RAAw5), .out6(RAAw6),
    .out7(RAAw7), .out8(RAAw8), .out9(RAAw9), .out10(RAAw10), .out11(RAAw11), .out12(RAAw12), .out13(RAAw13),
    .out14(RAAw14), .out15(RAAw15), .in(1'b1), .sel(Read_Address_A), .en(enable));
  Multiplexer #(.width(16)) multiplexer_1 (
    .in0(Write_Data), .in1(adder_1_out), .out(WD), .sel(IsCall_Return));  // open: en
  Multiplexer #(.width(4)) multiplexer_2 (
    .in0(Write_Address), .in1(Read_Address_B), .out(WA), .sel(IsCall_Return));  // open: en
  Multiplexer #(.width(16)) multiplexer_3 (.in0(WD), .in1(New_FP), .out(FP), .sel(IsCall_Return));  // open: en
  Swap_two_variables_using_XOR Swap (.in_1(out_9), .in_2(out_25), .New_Variable_1(New_RDA), .New_variable_2(New_FP));
  Multiplexer #(.select(4), .width(16), .disabled(0)) multiplexer_4 (
    .in0(out_11), .in1(out_14), .in2(out_16), .in3(out_18), .in4(out_20), .in5(out_22), .in6(out_24),
    .in7(out_26), .in8(out_10), .in9(out_15), .in10(out_17), .in11(out_19), .in12(out_21), .in13(out_23),
    .in14(out_25), .in15(out_27), .out(out_9), .sel(Read_Address_A));  // open: en
  Register #(.width(16)) R0 (.en(and_1_out), .Q(out_11), .clk(clock));  // open: D, clr
  and and_1 (and_1_out, 1'b1, w0);
  Register #(.width(16)) R1 (.D(WD), .en(and_2_out), .Q(out_14), .clk(clock));  // open: clr
  and and_2 (and_2_out, 1'b1, w1);
  Register #(.width(16)) R2 (.D(WD), .en(and_3_out), .Q(out_16), .clk(clock));  // open: clr
  and and_3 (and_3_out, 1'b1, w2);
  Register #(.width(16)) R3 (.D(WD), .en(and_4_out), .Q(out_18), .clk(clock));  // open: clr
  and and_4 (and_4_out, 1'b1, w3);
  Register #(.width(16)) R4 (.D(WD), .en(and_5_out), .Q(out_20), .clk(clock));  // open: clr
  and and_5 (and_5_out, 1'b1, w4);
  Register #(.width(16)) R5 (.D(WD), .en(and_6_out), .Q(out_22), .clk(clock));  // open: clr
  and and_6 (and_6_out, 1'b1, w5);
  Register #(.width(16)) R6 (.D(WD), .en(and_7_out), .Q(out_24), .clk(clock));  // open: clr
  and and_7 (and_7_out, 1'b1, w6);
  Register #(.width(16)) R7 (.D(WD), .en(and_8_out), .Q(out_26), .clk(clock));  // open: clr
  and and_8 (and_8_out, 1'b1, w7);
  Multiplexer #(.select(4), .width(16), .disabled(0)) multiplexer_5 (
    .in0(out_11), .in1(out_14), .in2(out_16), .in3(out_18), .in4(out_20), .in5(out_22), .in6(out_24),
    .in7(out_26), .in8(out_10), .in9(out_15), .in10(out_17), .in11(out_19), .in12(out_21), .in13(out_23),
    .in14(out_25), .in15(out_27), .out(out_13), .sel(WA));  // open: en
  and and_9 (and_9_out, 1'b1, w11);
  Multiplexer #(.select(2), .width(16)) multiplexer_6 (
    .in0(WD), .in1(WD), .in2(WD), .in3(New_RDA), .out(multiplexer_6_out), .sel({RAAw12, IsCall_Return}));  // open: en
  and and_10 (and_10_out, 1'b1, w12);
  and and_11 (and_11_out, IsCall_Return, RAAw12);
  and and_12 (and_12_out, 1'b1, w13);
  and and_13 (and_13_out, 1'b1, w14);
  Register #(.width(16)) R8 (.D(WD), .en(and_14_out), .Q(out_10), .clk(clock));  // open: clr
  and and_14 (and_14_out, 1'b1, w8);
  Register #(.width(16)) R9 (.D(WD), .en(and_15_out), .Q(out_15), .clk(clock));  // open: clr
  and and_15 (and_15_out, 1'b1, w9);
  Register #(.width(16)) R10 (.D(WD), .en(and_16_out), .Q(out_17), .clk(clock));  // open: clr
  and and_16 (and_16_out, 1'b1, w10);
  Register #(.width(16)) R11 (.D(WD), .en(and_9_out), .Q(out_19), .clk(clock));  // open: clr
  Register #(.width(16)) R12 (.D(multiplexer_6_out), .en(or_1_out), .Q(out_21), .clk(clock));  // open: clr
  or or_1 (or_1_out, and_10_out, and_11_out);
  Register #(.width(16)) R13 (.D(WD), .en(and_12_out), .Q(out_23), .clk(clock));  // open: clr
  Register #(.width(16)) R14 (.D(FP), .en(or_2_out), .Q(out_25), .clk(clock));  // open: clr
  or or_2 (or_2_out, and_13_out, IsCall_Return);
  Register #(.width(16)) R15 (.D(WD), .en(and_17_out), .Q(out_27), .clk(clock));  // open: clr
  and and_17 (and_17_out, 1'b1, w15);
  Multiplexer #(.select(4), .width(16), .disabled(0)) multiplexer_7 (
    .in0(out_11), .in1(out_14), .in2(out_16), .in3(out_18), .in4(out_20), .in5(out_22), .in6(out_24),
    .in7(out_26), .in8(out_10), .in9(out_15), .in10(out_17), .in11(out_19), .in12(out_21), .in13(out_23),
    .in14(out_25), .in15(out_27), .out(out_12), .sel(Read_Address_B));  // open: en

  // Other names for the same wires on the sheet: clk = clock; Normal_WA[3:0] = Write_Address;
  //   Normal_WD[15:0] = Write_Data; O0[15:0] = out_11; O1[15:0] = out_14; O2[15:0] = out_16; O3[15:0] = out_18;
  //   O4[15:0] = out_20; O5[15:0] = out_22; O6[15:0] = out_24; O7[15:0] = out_26; O8[15:0] = out_10;
  //   O9[15:0] = out_15; O10[15:0] = out_17; O11[15:0] = out_19; O12[15:0] = out_21; O13[15:0] = out_23;
  //   O14[15:0] = out_25; O15[15:0] = out_27; RAA[3:0] = Read_Address_A; RAB[3:0] = Read_Address_B;
  //   Read_Data_A[15:0] = out_9; Read_Data_B[15:0] = out_12; Read_Data_Destination[15:0] = out_13

  // Notes on the sheet:
  //   1110
endmodule

module RSTRF (
  input  [15:0] Destination_Data_where_flags_are_stored,
  output [4:0] Restored_Flags
);


  assign Restored_Flags = Destination_Data_where_flags_are_stored[4:0];

  // Other names for the same wires on the sheet: Flags[15:0] = Destination_Data_where_flags_are_stored
endmodule

module Flag_Manipulations (
  input  [3:0] Flag_op_and_v4,
  input  [3:0] v3__v2__v1__v0,
  input  [4:0] CurrentCBCVZSflags,
  output [4:0] New_CBCVZS_flags
);

  wire not_1_out, not_2_out, not_3_out, not_4_out, not_5_out;
  wire [4:0] FOFF_Result, FON_Result;

  or or_1 (FON_Result[4], CurrentCBCVZSflags[4], Flag_op_and_v4[0]);
  or or_2 (FON_Result[3], CurrentCBCVZSflags[3], v3__v2__v1__v0[3]);
  or or_3 (FON_Result[2], CurrentCBCVZSflags[2], v3__v2__v1__v0[2]);
  or or_4 (FON_Result[1], CurrentCBCVZSflags[1], v3__v2__v1__v0[1]);
  or or_5 (FON_Result[0], CurrentCBCVZSflags[0], v3__v2__v1__v0[0]);
  and and_1 (FOFF_Result[4], CurrentCBCVZSflags[4], not_1_out);
  not not_1 (not_1_out, Flag_op_and_v4[0]);
  and and_2 (FOFF_Result[3], CurrentCBCVZSflags[3], not_2_out);
  not not_2 (not_2_out, v3__v2__v1__v0[3]);
  and and_3 (FOFF_Result[2], CurrentCBCVZSflags[2], not_3_out);
  not not_3 (not_3_out, v3__v2__v1__v0[2]);
  and and_4 (FOFF_Result[1], CurrentCBCVZSflags[1], not_4_out);
  not not_4 (not_4_out, v3__v2__v1__v0[1]);
  and and_5 (FOFF_Result[0], CurrentCBCVZSflags[0], not_5_out);
  not not_5 (not_5_out, v3__v2__v1__v0[0]);
  Multiplexer #(.select(3), .width(5)) multiplexer_1 (
    .in0(FON_Result), .in1(CurrentCBCVZSflags), .in2({Flag_op_and_v4[0], v3__v2__v1__v0}),
    .in3(CurrentCBCVZSflags), .in4(FOFF_Result), .in5(CurrentCBCVZSflags),
    .in6({CurrentCBCVZSflags[4], v3__v2__v1__v0}), .in7(CurrentCBCVZSflags), .out(New_CBCVZS_flags),
    .sel(Flag_op_and_v4[3:1]));  // open: en

  // Other names for the same wires on the sheet: CurrentS = CurrentCBCVZSflags[0]; CurrentZ = CurrentCBCVZSflags[1];
  //   CurrentV = CurrentCBCVZSflags[2]; CurrentC = CurrentCBCVZSflags[3]; flag_op[2:0] = Flag_op_and_v4[3:1];
  //   FSET4_Result[4:0] = {CurrentCBCVZSflags[4], v3__v2__v1__v0};
  //   FSET5_Result[4:0] = {Flag_op_and_v4[0], v3__v2__v1__v0}; v0_s = v3__v2__v1__v0[0]; v1_z = v3__v2__v1__v0[1];
  //   v2_v = v3__v2__v1__v0[2]; v3_c = v3__v2__v1__v0[3]; CurrentCB = CurrentCBCVZSflags[4];
  //   v4_cb = Flag_op_and_v4[0]; NewCBCVZSflags[4:0] = New_CBCVZS_flags
endmodule

module Load_Store_flags (
  input  [15:0] in_1,
  input  [4:0] CurrentCBCVZSflags,
  output [4:0] NewCBCVZSflags
);

  nor nor_1 (NewCBCVZSflags[1], in_1[0], in_1[1], in_1[2], in_1[3], in_1[4], in_1[5], in_1[6], in_1[7], in_1[8], in_1[9], in_1[10], in_1[11], in_1[12], in_1[13], in_1[14], in_1[15]);

  assign {NewCBCVZSflags[4:2], NewCBCVZSflags[0]} = {CurrentCBCVZSflags[4:2], in_1[15]};

  // Other names for the same wires on the sheet: CurrentS = CurrentCBCVZSflags[0]; CurrentZ = CurrentCBCVZSflags[1];
  //   NewS = in_1[15]; ResultData[15:0] = in_1; NewZ = NewCBCVZSflags[1]; CurrentV = CurrentCBCVZSflags[2];
  //   CurrentC = CurrentCBCVZSflags[3]; CurrentCB = CurrentCBCVZSflags[4]
endmodule

module Swap_two_variables_using_XOR (
  input  [15:0] in_1,
  input  [15:0] in_2,
  output [15:0] New_Variable_1,
  output [15:0] New_variable_2
);

  wire [15:0] Variable_1t;

  assign Variable_1t = in_1 ^ in_2;  // XOR_Gate xor_1, 16 bits wide
  assign New_variable_2 = Variable_1t ^ in_2;  // XOR_Gate xor_2, 16 bits wide
  assign New_Variable_1 = Variable_1t ^ New_variable_2;  // XOR_Gate xor_3, 16 bits wide

  // Other names for the same wires on the sheet: Variable_1[15:0] = in_1; Variable_2[15:0] = in_2;
  //   Variable_2t[15:0] = New_variable_2
endmodule

module experimenting_kb_term (
  input  in_1,
  input  in_2
);

  wire button_1_out, clock_1_out;
  wire [6:0] keyboard_1_data;

  Clock clock_1 (.out(clock_1_out));
  Keyboard #(.buflen(64)) keyboard_1 (.clk(clock_1_out), .re(in_2), .data(keyboard_1_data));  // open: clr, avail
  TTY tty_1 (.data(keyboard_1_data), .clk(clock_1_out), .we(in_1), .clr(button_1_out));
  Button button_1 (.out(button_1_out));
endmodule
